# Fritzing sketch AFbook (saved by Fritzing 0.9.3b)

parts:
  Raspberry_Pi_Zero1 = Raspberry Pi Zero
  SparkFun_Simultaneous_RFID_Reader_-_M6E_Nano1 = SparkFun Simultaneous RFID Reader - M6E Nano [part_number=SEN-14066]
  U1 = LIPO-2000mAh [package=lipo-2000]  # not connected
  U2 = LIPO-2000mAh [package=lipo-2000]  # not connected
  Part1 = PowerBoost 500 Charger  # not connected
  S1 = Toggle Switch [package=THT]  # not connected
  Part2 = Logic Level Converter

nets:
  3V3: Raspberry_Pi_Zero1.3v3, SparkFun_Simultaneous_RFID_Reader_-_M6E_Nano1.VCC
  GND: Raspberry_Pi_Zero1.GND, SparkFun_Simultaneous_RFID_Reader_-_M6E_Nano1.GND
  N1: Raspberry_Pi_Zero1.GPIO15, Part2.RX_LV
  N2: Raspberry_Pi_Zero1.GPIO14, Part2.TX_LV
  N3: SparkFun_Simultaneous_RFID_Reader_-_M6E_Nano1.RX, Part2.RX_HV
  N4: SparkFun_Simultaneous_RFID_Reader_-_M6E_Nano1.TX, Part2.TX_HV

custom parts:
  SparkFun Simultaneous RFID Reader - M6E Nano: Description: The SparkFun Simultaneous RFID Reader is an Arduino-compatible board to get you started with the M6E Nano UHF RFID Reader. Radio Frequency Identification (RFID) is becoming popular everywhere for tracking practically everything. Whether you want to get started by adding an RFID reader on your toolbox with tags on all your tools or allowing access to the tree house for your secret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
